// Logisim project BCDto7Segggggs__CLOCK.circ as structural Verilog: 3 circuits, main circuit BCD_to
module BCD_to (
  input  s0,
  input  s1,
  input  s2,
  input  s3,
  output out_5,
  output out_6,
  output out_7,
  output out_8,
  output out_9,
  output out_10,
  output out_11
);

  wire and_1_out, and_2_out, and_3_out, and_4_out, and_5_out, and_6_out, and_7_out, and_8_out, and_9_out,
       and_10_out, and_11_out, and_12_out, and_13_out, and_14_out, and_15_out, and_16_out, not_1_out,
       not_2_out, not_3_out;

  not not_1 (not_1_out, s1);
  not not_2 (not_2_out, s2);
  not not_3 (not_3_out, s3);
  and and_1 (and_1_out, not_1_out, not_3_out);
  and and_2 (and_2_out, s1, s3);
  and and_3 (and_3_out, not_2_out, not_3_out);
  and and_4 (and_4_out, s2, s3);
  or or_1 (out_7, not_2_out, s3, s1);
  and and_5 (and_5_out, not_1_out, not_3_out);
  and and_6 (and_6_out, not_1_out, s2);
  and and_7 (and_7_out, s1, not_2_out, s3);
  and and_8 (and_8_out, s2, not_3_out);
  and and_9 (and_9_out, not_1_out, not_3_out);
  and and_10 (and_10_out, s2, not_3_out);
  and and_11 (and_11_out, not_2_out, not_3_out);
  and and_12 (and_12_out, s1, not_2_out);
  and and_13 (and_13_out, s1, not_3_out);
  and and_14 (and_14_out, not_1_out, s2);
  and and_15 (and_15_out, s1, not_2_out);
  and and_16 (and_16_out, s2, not_3_out);
  or or_2 (out_5, and_1_out, s2, and_2_out, s0);
  or or_3 (out_6, not_1_out, and_3_out, and_4_out);
  or or_4 (out_8, and_5_out, and_6_out, and_7_out, and_8_out, s0);
  or or_5 (out_9, and_9_out, and_10_out);
  or or_6 (out_10, and_11_out, and_12_out, and_13_out, s0);
  or or_7 (out_11, and_14_out, and_15_out, s0, and_16_out);
endmodule

module bc (
  input  [1:0] in_1,
  input  [1:0] in_2
);

  BCD_to bcd_to_1 ();  // open: s0, s1, s2, s3, out_5, out_6, out_7, out_8, out_9, out_10, out_11
endmodule

module bcd (
);

  wire bcd_to_1_out_5, bcd_to_1_out_6, bcd_to_1_out_7, bcd_to_1_out_8, bcd_to_1_out_9, bcd_to_1_out_10,
       bcd_to_1_out_11, clk1_out, clk2_out, clk3_out, clk4_out;

  Clock #(.highDuration(8), .lowDuration(8), .phaseOffset(1)) clk4 (.out(clk4_out));
  Clock #(.highDuration(4), .lowDuration(4), .phaseOffset(1)) clk3 (.out(clk3_out));
  Clock #(.highDuration(2), .lowDuration(2), .phaseOffset(1)) clk2 (.out(clk2_out));
  Clock #(.phaseOffset(1)) clk1 (.out(clk1_out));
  BCD_to bcd_to_1 (
    .s0(clk4_out), .s1(clk3_out), .s2(clk2_out), .s3(clk1_out), .out_5(bcd_to_1_out_5),
    .out_6(bcd_to_1_out_6), .out_7(bcd_to_1_out_7), .out_8(bcd_to_1_out_8), .out_9(bcd_to_1_out_9),
    .out_10(bcd_to_1_out_10), .out_11(bcd_to_1_out_11));
  _7_Segment_Display u_7_segment_display_1 (
    .g(bcd_to_1_out_11), .f(bcd_to_1_out_10), .a(bcd_to_1_out_5), .b(bcd_to_1_out_6), .e(bcd_to_1_out_9),
    .d(bcd_to_1_out_8), .c(bcd_to_1_out_7));  // open: dp
endmodule
