// Logisim project Lab4(Mux-Adder).circ as structural Verilog: 9 circuits, main circuit Mux21bit
module Mux21bit (
  input  s,
  input  s1,
  input  s2,
  output Ou
);

  wire and_1_out, and_2_out, not_1_out;

  not not_1 (not_1_out, s);
  and and_1 (and_1_out, not_1_out, s1);
  and and_2 (and_2_out, s, s2);
  or or_1 (Ou, and_1_out, and_2_out);
endmodule

module DongGoiMux21bit (
  input  in_1,
  input  in_2,
  input  in_3,
  output out_4
);

  Mux21bit mux21bit_1 (.s(in_1), .s1(in_2), .s2(in_3), .Ou(out_4));
endmodule

module Mux24bit (
  input  S,
  input  A3,
  input  B3,
  input  A2,
  input  B2,
  input  A1,
  input  B1,
  input  A0,
  input  B0,
  output F3,
  output F2,
  output F1,
  output F0
);

  Mux21bit mux21bit_1 (.s(S), .s1(A3), .s2(B3), .Ou(F3));
  Mux21bit mux21bit_2 (.s(S), .s1(A2), .s2(B2), .Ou(F2));
  Mux21bit mux21bit_3 (.s(S), .s1(A1), .s2(B1), .Ou(F1));
  Mux21bit mux21bit_4 (.s(S), .s1(A0), .s2(B0), .Ou(F0));
endmodule

module DongGoiMux24bit (
  input  in_1,
  input  in_2,
  input  in_3,
  input  in_4,
  input  in_5,
  input  in_6,
  input  in_7,
  input  in_8,
  input  in_9,
  output out_10,
  output out_11,
  output out_12,
  output out_13
);

  Mux24bit mux24bit_1 (
    .S(in_1), .A3(in_2), .B3(in_3), .A2(in_4), .B2(in_5), .A1(in_6), .B1(in_7), .A0(in_8), .B0(in_9),
    .F3(out_10), .F2(out_11), .F1(out_12), .F0(out_13));
endmodule

module Mux44bit (
  input  S_0,
  input  S_1,
  input  A1_3,
  input  B1_3,
  input  A1_2,
  input  B1_2,
  input  A1_1,
  input  B1_1,
  input  A1_0,
  input  B1_0,
  input  A0_3,
  input  B0_3,
  input  A0_2,
  input  B0_2,
  input  A0_1,
  input  B0_1,
  input  A0_0,
  input  B0_0,
  output F3,
  output F2,
  output F1,
  output F0
);

  wire mux24bit_1_f0, mux24bit_1_f1, mux24bit_1_f2, mux24bit_1_f3, mux24bit_2_f0, mux24bit_2_f1,
       mux24bit_2_f2, mux24bit_2_f3;

  Mux24bit mux24bit_1 (
    .S(S_0), .A3(A1_3), .B3(B1_3), .A2(A1_2), .B2(B1_2), .A1(A1_1), .B1(B1_1), .A0(A1_0), .B0(B1_0),
    .F3(mux24bit_1_f3), .F2(mux24bit_1_f2), .F1(mux24bit_1_f1), .F0(mux24bit_1_f0));
  Mux24bit mux24bit_2 (
    .S(S_0), .A3(A0_3), .B3(B0_3), .A2(A0_2), .B2(B0_2), .A1(A0_1), .B1(B0_1), .A0(A0_0), .B0(B0_0),
    .F3(mux24bit_2_f3), .F2(mux24bit_2_f2), .F1(mux24bit_2_f1), .F0(mux24bit_2_f0));
  Mux24bit mux24bit_3 (
    .S(S_1), .A3(mux24bit_1_f3), .B3(mux24bit_2_f3), .A2(mux24bit_1_f2), .B2(mux24bit_2_f2),
    .A1(mux24bit_1_f1), .B1(mux24bit_2_f1), .A0(mux24bit_1_f0), .B0(mux24bit_2_f0), .F3(F3), .F2(F2),
    .F1(F1), .F0(F0));
endmodule

module DongGoiMux44bit (
  input  S_0,
  input  S_1,
  input  A1_3,
  input  B1_3,
  input  A1_2,
  input  B1_2,
  input  A1_1,
  input  B1_1,
  input  A1_0,
  input  B1_0,
  input  A0_3,
  input  B0_3,
  input  A0_2,
  input  B0_2,
  input  A0_1,
  input  B0_1,
  input  A0_0,
  input  B0_0,
  output out_19,
  output out_20,
  output out_21,
  output out_22
);

  Mux44bit mux44bit_1 (
    .S_0(S_0), .S_1(S_1), .A1_3(A1_3), .B1_3(B1_3), .A1_2(A1_2), .B1_2(B1_2), .A1_1(A1_1), .B1_1(B1_1),
    .A1_0(A1_0), .B1_0(B1_0), .A0_3(A0_3), .B0_3(B0_3), .A0_2(A0_2), .B0_2(B0_2), .A0_1(A0_1), .B0_1(B0_1),
    .A0_0(A0_0), .B0_0(B0_0), .F3(out_19), .F2(out_20), .F1(out_21), .F0(out_22));
endmodule

module FullAdder (
  input  C_in,
  input  A,
  input  B,
  output S,
  output C_out
);

  wire and_1_out, and_2_out, or_1_out, xor_1_out;

  and and_1 (and_1_out, A, B);
  or or_1 (or_1_out, A, B);
  xor xor_1 (xor_1_out, C_in, A);
  and and_2 (and_2_out, or_1_out, C_in);
  xor xor_2 (S, xor_1_out, B);
  or or_2 (C_out, and_1_out, and_2_out);
endmodule

module DongGoiMachCongToanPhan (
  input  Cin,
  input  A,
  input  B,
  output S,
  output Cout
);

  FullAdder fulladder_1 (.C_in(Cin), .A(A), .B(B), .S(S), .C_out(Cout));
endmodule

module BoCong4bit (
  input  C0,
  input  A0,
  input  B0,
  input  A1,
  input  B1,
  input  A2,
  input  B2,
  input  A3,
  input  B3,
  output S0,
  output S1,
  output S2,
  output S3,
  output C3
);

  wire fulladder_1_c_out, fulladder_2_c_out, fulladder_3_c_out;

  FullAdder fulladder_1 (.C_in(C0), .A(A0), .B(B0), .S(S0), .C_out(fulladder_1_c_out));
  FullAdder fulladder_2 (.C_in(fulladder_1_c_out), .A(A1), .B(B1), .S(S1), .C_out(fulladder_2_c_out));
  FullAdder fulladder_3 (.C_in(fulladder_2_c_out), .A(A2), .B(B2), .S(S2), .C_out(fulladder_3_c_out));
  FullAdder fulladder_4 (.C_in(fulladder_3_c_out), .A(A3), .B(B3), .S(S3), .C_out(C3));
endmodule
