// Logisim project Mux_Plus_Compare.circ as structural Verilog: 6 circuits, main circuit BCD_2_7_SEG
module BCD_2_7_SEG (
  input  I3,
  input  I2,
  input  I1,
  input  I0,
  output A,
  output B,
  output C,
  output D,
  output E,
  output F,
  output G
);

  wire and_1_out, and_2_out, and_3_out, and_4_out, and_5_out, and_6_out, and_7_out, and_8_out, and_9_out,
       and_10_out, and_11_out, and_12_out, and_13_out, and_14_out, and_15_out, and_16_out, and_17_out,
       not_1_out, not_2_out, not_3_out, or_1_out, or_2_out, or_3_out, or_4_out, or_6_out, or_8_out, or_9_out,
       or_10_out, or_11_out, or_14_out, or_15_out;

  not not_1 (not_1_out, I2);
  not not_2 (not_2_out, I1);
  not not_3 (not_3_out, I0);
  and and_1 (and_1_out, not_1_out, not_3_out);
  and and_2 (and_2_out, I2, I0);
  and and_3 (and_3_out, not_2_out, not_3_out);
  or or_1 (or_1_out, not_2_out, I0);
  and and_4 (and_4_out, not_1_out, not_3_out);
  and and_5 (and_5_out, not_1_out, I1);
  and and_6 (and_6_out, I2, not_2_out);
  and and_7 (and_7_out, not_1_out, not_3_out);
  and and_8 (and_8_out, I1, not_3_out);
  and and_9 (and_9_out, not_2_out, not_3_out);
  and and_10 (and_10_out, I2, not_2_out);
  and and_11 (and_11_out, I2, not_3_out);
  and and_12 (and_12_out, not_1_out, I1);
  and and_13 (and_13_out, I2, not_2_out);
  and and_14 (and_14_out, I1, not_3_out);
  or or_2 (or_2_out, and_1_out, I1);
  or or_3 (or_3_out, and_2_out, I3);
  or or_4 (or_4_out, not_1_out, and_3_out);
  and and_15 (and_15_out, I1, I0);
  or or_5 (C, or_1_out, I2);
  or or_6 (or_6_out, and_4_out, and_5_out);
  and and_16 (and_16_out, and_6_out, I0);
  and and_17 (and_17_out, I1, not_3_out);
  or or_7 (E, and_7_out, and_8_out);
  or or_8 (or_8_out, and_9_out, and_10_out);
  or or_9 (or_9_out, and_11_out, I3);
  or or_10 (or_10_out, and_12_out, and_13_out);
  or or_11 (or_11_out, I3, and_14_out);
  or or_12 (A, or_2_out, or_3_out);
  or or_13 (B, or_4_out, and_15_out);
  or or_14 (or_14_out, or_6_out, and_16_out);
  or or_15 (or_15_out, and_17_out, I3);
  or or_16 (F, or_8_out, or_9_out);
  or or_17 (G, or_10_out, or_11_out);
  or or_18 (D, or_14_out, or_15_out);
endmodule

module MUX2to1 (
  input  D4,
  input  D3,
  input  D2,
  input  D1,
  input  S0,
  input  S1,
  output Y
);

  wire bcd_2_7_seg_1_a, bcd_2_7_seg_2_a;

  BCD_2_7_SEG bcd_2_7_seg_1 (.I3(D4), .I2(S0), .I1(D3), .A(bcd_2_7_seg_1_a));  // open: I0, B, C, D, E, F, G
  BCD_2_7_SEG bcd_2_7_seg_2 (.I3(D2), .I2(S0), .I1(D1), .A(bcd_2_7_seg_2_a));  // open: I0, B, C, D, E, F, G
  BCD_2_7_SEG bcd_2_7_seg_3 (.I3(bcd_2_7_seg_1_a), .I2(S1), .I1(bcd_2_7_seg_2_a), .A(Y));  // open: I0, B, C, D, E, F, G
endmodule

module MUX4to1 (
  input  EN,
  input  A,
  input  B,
  output LT,
  output EQ,
  output GT
);

  wire and_2_out, and_3_out, not_1_out, not_2_out, not_3_out, not_4_out;

  not not_1 (not_1_out, A);
  not not_2 (not_2_out, A);
  not not_3 (not_3_out, B);
  not not_4 (not_4_out, B);
  and and_1 (LT, EN, not_1_out, B);
  and and_2 (and_2_out, EN, not_2_out, not_3_out);
  and and_3 (and_3_out, EN, A, B);
  and and_4 (GT, EN, A, not_4_out);
  or or_1 (EQ, and_2_out, and_3_out);
endmodule

module MACHsosanh1BIT (
  input  A0,
  input  B0,
  input  A1,
  input  B1,
  input  A2,
  input  B2,
  input  EN3,
  input  A3,
  input  B3,
  output EQ,
  output LT,
  output GT
);

  wire mux4to1_1_gt, mux4to1_1_lt, mux4to1_2_eq, mux4to1_2_gt, mux4to1_2_lt, mux4to1_3_eq, mux4to1_3_gt,
       mux4to1_3_lt, mux4to1_4_eq, mux4to1_4_gt, mux4to1_4_lt;

  MUX4to1 mux4to1_1 (.EN(mux4to1_2_eq), .A(A0), .B(B0), .LT(mux4to1_1_lt), .EQ(EQ), .GT(mux4to1_1_gt));
  MUX4to1 mux4to1_2 (.EN(mux4to1_3_eq), .A(A1), .B(B1), .LT(mux4to1_2_lt), .EQ(mux4to1_2_eq), .GT(mux4to1_2_gt));
  MUX4to1 mux4to1_3 (.EN(mux4to1_4_eq), .A(A2), .B(B2), .LT(mux4to1_3_lt), .EQ(mux4to1_3_eq), .GT(mux4to1_3_gt));
  MUX4to1 mux4to1_4 (.EN(EN3), .A(A3), .B(B3), .LT(mux4to1_4_lt), .EQ(mux4to1_4_eq), .GT(mux4to1_4_gt));
  or or_1 (LT, mux4to1_1_lt, mux4to1_2_lt, mux4to1_3_lt, mux4to1_4_lt);
  or or_2 (GT, mux4to1_1_gt, mux4to1_2_gt, mux4to1_3_gt, mux4to1_4_gt);
endmodule

module MACHsosanh4BIT (
  input  A,
  input  B,
  input  Cin,
  output SUM,
  output COUT
);

  wire and_1_out, and_2_out, and_3_out, and_4_out, and_5_out, and_6_out, and_7_out, not_1_out, not_2_out,
       not_3_out;

  not not_1 (not_1_out, A);
  not not_2 (not_2_out, B);
  not not_3 (not_3_out, Cin);
  and and_1 (and_1_out, not_1_out, not_2_out, Cin);
  and and_2 (and_2_out, not_1_out, B, not_3_out);
  and and_3 (and_3_out, A, not_2_out, not_3_out);
  and and_4 (and_4_out, A, Cin);
  and and_5 (and_5_out, B, Cin);
  and and_6 (and_6_out, A, Cin);
  and and_7 (and_7_out, A, B);
  or or_1 (SUM, and_1_out, and_2_out, and_3_out, and_4_out);
  or or_2 (COUT, and_5_out, and_6_out, and_7_out);
endmodule

module MACHcong4BIT (
  input  [3:0] in_1,
  input  in_2,
  input  [3:0] in_3
);

  wire bcd_2_7_seg_1_a, bcd_2_7_seg_1_b, bcd_2_7_seg_1_c, bcd_2_7_seg_1_d, bcd_2_7_seg_1_e, bcd_2_7_seg_1_f,
       bcd_2_7_seg_1_g, bcd_2_7_seg_2_a, bcd_2_7_seg_2_b, bcd_2_7_seg_2_c, bcd_2_7_seg_2_d, bcd_2_7_seg_2_e,
       bcd_2_7_seg_2_f, bcd_2_7_seg_2_g, machsosanh4bit_2_cout, machsosanh4bit_3_cout, machsosanh4bit_4_cout,
       n7_segment_display_1_p1, n7_segment_display_2_p1, n7_segment_display_3_p1, n7_segment_display_4_p1;
  wire [3:0] binary_to_bcd_converter_3_p2, binary_to_bcd_converter_3_p3, machsosanh4bit_4_sum;
  wire [4:4] machsosanh4bit_1_cout;

  // _7_Segment_Display 7_segment_display_1: pin names not known; wires that end beside it: n7_segment_display_1_p1, n7_segment_display_1_p1
  // BCD_to_7_Segment_decoder bcd_to_7_segment_decoder_1: pin names not known
  // Binary_to_BCD_converter #(.binvalue(4)) binary_to_bcd_converter_1: pin names not known; wires that end beside it: in_1
  // _7_Segment_Display 7_segment_display_2: pin names not known; wires that end beside it: n7_segment_display_2_p1, n7_segment_display_2_p1
  // BCD_to_7_Segment_decoder bcd_to_7_segment_decoder_2: pin names not known
  // _7_Segment_Display 7_segment_display_3: pin names not known; wires that end beside it: n7_segment_display_3_p1, n7_segment_display_3_p1
  // _7_Segment_Display 7_segment_display_4: pin names not known; wires that end beside it: n7_segment_display_4_p1, n7_segment_display_4_p1
  // BCD_to_7_Segment_decoder bcd_to_7_segment_decoder_3: pin names not known
  // BCD_to_7_Segment_decoder bcd_to_7_segment_decoder_4: pin names not known
  // Binary_to_BCD_converter #(.binvalue(4)) binary_to_bcd_converter_2: pin names not known; wires that end beside it: in_3
  MACHsosanh4BIT machsosanh4bit_1 (
    .A(in_1[3]), .B(in_3[3]), .Cin(machsosanh4bit_2_cout), .SUM(machsosanh4bit_4_sum[3]),
    .COUT(machsosanh4bit_1_cout[4]));
  MACHsosanh4BIT machsosanh4bit_2 (
    .A(in_1[2]), .B(in_3[2]), .Cin(machsosanh4bit_3_cout), .SUM(machsosanh4bit_4_sum[2]),
    .COUT(machsosanh4bit_2_cout));
  MACHsosanh4BIT machsosanh4bit_3 (
    .A(in_1[1]), .B(in_3[1]), .Cin(machsosanh4bit_4_cout), .SUM(machsosanh4bit_4_sum[1]),
    .COUT(machsosanh4bit_3_cout));
  MACHsosanh4BIT machsosanh4bit_4 (
    .A(in_1[0]), .B(in_3[0]), .Cin(in_2), .SUM(machsosanh4bit_4_sum[0]), .COUT(machsosanh4bit_4_cout));
  // Binary_to_BCD_converter #(.binvalue(5)) binary_to_bcd_converter_3: pin names not known; wires that end beside it: {machsosanh4bit_1_cout[4], machsosanh4bit_4_sum}, binary_to_bcd_converter_3_p2, binary_to_bcd_converter_3_p3
  BCD_2_7_SEG bcd_2_7_seg_1 (
    .I3(binary_to_bcd_converter_3_p2[3]), .I2(binary_to_bcd_converter_3_p2[2]),
    .I1(binary_to_bcd_converter_3_p2[1]), .I0(binary_to_bcd_converter_3_p2[0]), .A(bcd_2_7_seg_1_a),
    .B(bcd_2_7_seg_1_b), .C(bcd_2_7_seg_1_c), .D(bcd_2_7_seg_1_d), .E(bcd_2_7_seg_1_e), .F(bcd_2_7_seg_1_f),
    .G(bcd_2_7_seg_1_g));
  BCD_2_7_SEG bcd_2_7_seg_2 (
    .I3(binary_to_bcd_converter_3_p3[3]), .I2(binary_to_bcd_converter_3_p3[2]),
    .I1(binary_to_bcd_converter_3_p3[1]), .I0(binary_to_bcd_converter_3_p3[0]), .A(bcd_2_7_seg_2_a),
    .B(bcd_2_7_seg_2_b), .C(bcd_2_7_seg_2_c), .D(bcd_2_7_seg_2_d), .E(bcd_2_7_seg_2_e), .F(bcd_2_7_seg_2_f),
    .G(bcd_2_7_seg_2_g));
  _7_Segment_Display u_7_segment_display_5 (
    .g(bcd_2_7_seg_1_g), .f(bcd_2_7_seg_1_f), .a(bcd_2_7_seg_1_a), .b(bcd_2_7_seg_1_b), .e(bcd_2_7_seg_1_e),
    .d(bcd_2_7_seg_1_d), .c(bcd_2_7_seg_1_c));  // open: dp
  _7_Segment_Display u_7_segment_display_6 (
    .g(bcd_2_7_seg_2_g), .f(bcd_2_7_seg_2_f), .a(bcd_2_7_seg_2_a), .b(bcd_2_7_seg_2_b), .e(bcd_2_7_seg_2_e),
    .d(bcd_2_7_seg_2_d), .c(bcd_2_7_seg_2_c));  // open: dp
endmodule
