// Logisim project machcong.circ as structural Verilog: 1 circuit, main circuit main
module main (
  input  [1:0] in_1,
  input  [1:0] in_2
);

  wire adder_1_cout, n7447_1_pin2, n7447_1_pin9, n7447_1_pin10, n7447_1_pin11, n7447_1_pin12, n7447_1_pin13,
       n7447_1_pin14, n7447_1_pin15, n7447_2_pin9, n7447_2_pin10, n7447_2_pin11, n7447_2_pin12,
       n7447_2_pin13, n7447_2_pin14, n7447_2_pin15, n7447_3_pin6, n7447_3_pin9, n7447_3_pin10, n7447_3_pin11,
       n7447_3_pin12, n7447_3_pin13, n7447_3_pin14, n7447_3_pin15;
  wire [1:0] adder_1_out;

  _7447 #(.ShowInternalStructure("true")) u_7447_1 (
    .pin1(in_1[1]), .pin2(n7447_1_pin2), .pin6(n7447_1_pin2), .pin7(in_1[0]), .pin15(n7447_1_pin15),
    .pin14(n7447_1_pin14), .pin13(n7447_1_pin13), .pin12(n7447_1_pin12), .pin11(n7447_1_pin11),
    .pin10(n7447_1_pin10), .pin9(n7447_1_pin9));  // open: pin3, pin4, pin5
  _7447 #(.ShowInternalStructure("true")) u_7447_2 (
    .pin1(in_2[1]), .pin2(n7447_1_pin2), .pin6(n7447_1_pin2), .pin7(in_2[0]), .pin15(n7447_2_pin15),
    .pin14(n7447_2_pin14), .pin13(n7447_2_pin13), .pin12(n7447_2_pin12), .pin11(n7447_2_pin11),
    .pin10(n7447_2_pin10), .pin9(n7447_2_pin9));  // open: pin3, pin4, pin5
  _7_Segment_Display #(.active("false")) u_7_segment_display_1 (
    .g(n7447_1_pin14), .f(n7447_1_pin15), .a(n7447_1_pin13), .b(n7447_1_pin12), .e(n7447_1_pin9),
    .d(n7447_1_pin10), .c(n7447_1_pin11));  // open: dp
  _7_Segment_Display #(.active("false")) u_7_segment_display_2 (
    .g(n7447_2_pin14), .f(n7447_2_pin15), .a(n7447_2_pin13), .b(n7447_2_pin12), .e(n7447_2_pin9),
    .d(n7447_2_pin10), .c(n7447_2_pin11));  // open: dp
  Adder #(.width(2)) adder_1 (.a(in_1), .b(in_2), .out(adder_1_out), .cout(adder_1_cout));  // open: cin
  _7447 #(.ShowInternalStructure("true")) u_7447_3 (
    .pin1(adder_1_out[1]), .pin2(adder_1_cout), .pin6(n7447_3_pin6), .pin7(adder_1_out[0]),
    .pin15(n7447_3_pin15), .pin14(n7447_3_pin14), .pin13(n7447_3_pin13), .pin12(n7447_3_pin12),
    .pin11(n7447_3_pin11), .pin10(n7447_3_pin10), .pin9(n7447_3_pin9));  // open: pin3, pin4, pin5
  _7_Segment_Display #(.active("false")) u_7_segment_display_3 (
    .g(n7447_3_pin14), .f(n7447_3_pin15), .a(n7447_3_pin13), .b(n7447_3_pin12), .e(n7447_3_pin9),
    .d(n7447_3_pin10), .c(n7447_3_pin11));  // open: dp
  // also tied to GND on the sheet: {n7447_1_pin2, n7447_3_pin6}
endmodule
